# Fritzing sketch SanguinoBB (saved by Fritzing 0.7.5b)
breadboards: 1

parts:
  Arduino2 = Arduino
  XTAL1 = Crystal [frequency="16 Mhz" package=THT]
  Part1 = FTDI Basic Programmer  # not connected
  Atmega1 = ATmega644 [package=pdpi]
  S2 = Pushbutton [package="[THT]"]
  C1 = Ceramic Capacitor [capacitance=20pF package="200 mil [THT, multilayer]"]
  C2 = Ceramic Capacitor [capacitance=20pF package="200 mil [THT, multilayer]"]

nets:
  N1: Arduino2.+5V, Atmega1.AVCC, Atmega1.AREF
  N2: Arduino2.GND, Atmega1.GND#30
  N3: XTAL1.pin_0, Atmega1.XTAL1, C2.1
  N4: XTAL1.pin_1, Atmega1.XTAL2, C1.0
  N5: Atmega1.RESET, S2.Pin_1, S2.Pin_2
  N6: S2.Pin_3, S2.Pin_4
  N7: C1.1, C2.0
